# Fritzing sketch mySafeUV_Breadboard (saved by Fritzing 0.9.3b)
breadboards: 1

parts:
  Raspberry_Pi_1 = Raspberry Pi 3 [part_number=RPI-3-V1.2]
  SCL1 = VEML6070 [part_number=VEML6070]

nets:
  N1: Raspberry_Pi_1.GPIO2, SCL1.SDA
  N2: Raspberry_Pi_1.GPIO3, SCL1.SCL
  GND: Raspberry_Pi_1.GND, SCL1.GND
  5V: Raspberry_Pi_1.5V, SCL1.VDD

custom parts:
  VEML6070: This little sensor is a great way to add UV light sensing to any microcontroller project. The VEML6070 from Vishay has a true UV A light sensor and an I2C-controlled ADC that will take readings and integrate them for you over ~60ms to 500ms.
